// Digital circuit Decoder.dig as structural Verilog
module Decoder (
  input  [31:0] Instruction,
  output [15:0] A,
  output [1:0] rs,
  output [1:0] rd
);


  assign A = Instruction[15:0];
  assign rd = Instruction[21:20];
  assign rs = Instruction[17:16];
endmodule
