// Digital circuit Execute.dig as structural Verilog
module Execute (
  input  [15:0] B,
  input  [15:0] A,
  output [15:0] Result,
  output Carry
);

  Add #(.Bits(16)) add_1 (.a(A), .b(B), .c_i(1'b0), .s(Result), .c_o(Carry));
endmodule
