// Digital circuit cpu2.dig as structural Verilog
module cpu2 (
  input  in_1,
  input  in_2,
  input  in_3,
  input  in_4,
  input  in_13,
  input  in_14,
  input  in_17,
  input  in_19,
  input  clk,
  input  in_31,
  input  in_34,
  output out_5,
  output Incrament,
  output Fetch,
  output Execute,
  output Decocde,
  output out_10,
  output out_11,
  output out_12,
  output out_15,
  output out_16,
  output out_18,
  output out_20,
  output out_21,
  output out_22,
  output out_23,
  output out_24,
  output out_25,
  output out_26,
  output out_27,
  output out_28,
  output out_29,
  output out_32,
  output out_33,
  output out_35,
  output out_36,
  output out_37,
  output out_38,
  output out_39,
  output out_40,
  output out_41,
  output out_42
);

  wire add_1_c_o, and_1_out, and_2_out, and_3_out, and_4_out, and_5_out, and_6_out, and_7_out, and_8_out,
       and_9_out, and_10_out, and_11_out, and_12_out, and_13_out, and_14_out, and_15_out, and_16_out,
       and_17_out, and_18_out, and_19_out, and_20_out, and_21_out, and_22_out, and_23_out, and_24_out,
       and_25_out, and_26_out, and_27_out, and_28_out, and_29_out, and_30_out, and_31_out, and_32_out,
       and_33_out, and_34_out, and_51_out, and_52_out, and_53_out, and_54_out, and_55_out, and_56_out,
       and_57_out, and_58_out, and_59_out, d_ff_1_q, d_ff_as_7_q, nor_1_out, nor_2_out, nor_3_out, nor_4_out,
       not_1_out, not_2_out, not_3_out, not_4_out, not_5_out, not_6_out, not_7_out, not_8_out, not_9_out,
       not_10_out, not_11_out, not_12_out, not_13_out, not_14_out, not_15_out, not_16_out, not_17_out,
       not_18_out, not_19_out, not_20_out, not_21_out, not_22_out, not_23_out, not_24_out, not_25_out,
       not_26_out, not_27_out, not_28_out, not_29_out, not_30_out, not_32_out, not_34_out, not_35_out,
       not_36_out, not_37_out, not_38_out, not_39_out, not_40_out, not_41_out, not_42_out, not_43_out,
       not_44_out, not_45_out, not_46_out, not_47_out, not_48_out, not_49_out, not_50_out, not_51_out,
       not_52_out, not_53_out, not_54_out, not_55_out, not_56_out, not_57_out, not_58_out, not_59_out,
       not_60_out, not_61_out, not_62_out, not_63_out, not_64_out, not_65_out, or_1_out, or_2_out, or_3_out,
       or_4_out, or_5_out, or_6_out, or_7_out, or_8_out, or_9_out, or_10_out, or_11_out, or_12_out,
       xor_1_out, xor_2_out, xor_3_out, xor_4_out, xor_5_out, xor_6_out, xor_7_out, xor_8_out;
  wire [1:0] not_31_out;
  wire [7:0] add_1_s, and_42_out, and_50_out, multiplexer_1_out, multiplexer_2_out, multiplexer_3_out,
       multiplexer_4_out, not_66_out, register_1_q;
  wire [15:0] blockramdualport_1_d, register_2_q;

  D_FF d_ff_1 (.D(in_19), .C(or_12_out), .Q(d_ff_1_q), .nQ(out_18));
  // Probe on blockramdualport_1_d[15:8]
  Register #(.Bits(8), .isProgramCounter("true")) register_1 (
    .D(multiplexer_3_out), .C(or_12_out), .en(or_11_out), .Q(register_1_q));
  Register #(.Bits(16)) register_2 (
    .D(blockramdualport_1_d), .C(or_12_out), .en(not_47_out),
    .Q({register_2_q[15:10], out_23, out_24, register_2_q[7:0]}));
  or or_1 (or_1_out, and_16_out, and_25_out, and_26_out);
  and and_1 (and_1_out, 1'b1, or_12_out);
  and and_2 (and_2_out, 1'b1, or_12_out);
  and and_3 (and_3_out, or_1_out, or_12_out);
  D_FF_AS d_ff_as_1 (.Set(in_14), .D(add_1_c_o), .C(and_2_out), .Clr(d_ff_1_q), .Q(out_20), .nQ(out_15));
  D_FF_AS d_ff_as_2 (.Set(in_13), .D(and_51_out), .C(and_3_out), .Clr(d_ff_1_q), .Q(out_21), .nQ(out_16));
  D_FF_AS #(.Default(1)) d_ff_as_3 (.Set(d_ff_1_q), .D(Incrament), .C(and_1_out), .Clr(in_1), .Q(Fetch), .nQ(out_12));
  or or_2 (or_2_out, Decocde, Execute);
  and and_4 (and_4_out, register_2_q[15], not_1_out, register_2_q[13], not_2_out);
  not not_1 (not_1_out, register_2_q[14]);
  not not_2 (not_2_out, register_2_q[12]);
  and and_5 (and_5_out, register_2_q[15], register_2_q[14], register_2_q[13], not_3_out);
  not not_3 (not_3_out, register_2_q[12]);
  and and_6 (and_6_out, not_4_out, not_5_out, not_6_out, not_7_out);
  not not_4 (not_4_out, register_2_q[15]);
  not not_5 (not_5_out, register_2_q[14]);
  not not_6 (not_6_out, register_2_q[13]);
  not not_7 (not_7_out, register_2_q[12]);
  and and_7 (and_7_out, not_8_out, register_2_q[14], not_9_out, not_10_out);
  not not_8 (not_8_out, register_2_q[15]);
  not not_9 (not_9_out, register_2_q[13]);
  not not_10 (not_10_out, register_2_q[12]);
  and and_8 (and_8_out, register_2_q[15], not_11_out, not_12_out, not_13_out);
  not not_11 (not_11_out, register_2_q[14]);
  not not_12 (not_12_out, register_2_q[13]);
  not not_13 (not_13_out, register_2_q[12]);
  and and_9 (and_9_out, register_2_q[15], not_14_out, not_15_out, register_2_q[12]);
  not not_14 (not_14_out, register_2_q[14]);
  not not_15 (not_15_out, register_2_q[13]);
  and and_10 (and_10_out, not_16_out, register_2_q[14], register_2_q[13], not_17_out);
  not not_16 (not_16_out, register_2_q[15]);
  not not_17 (not_17_out, register_2_q[12]);
  and and_11 (and_11_out, not_18_out, not_19_out, not_20_out, register_2_q[12]);
  not not_18 (not_18_out, register_2_q[15]);
  not not_19 (not_19_out, register_2_q[14]);
  not not_20 (not_20_out, register_2_q[13]);
  D_FF_AS d_ff_as_4 (.Set(in_2), .D(Fetch), .C(and_1_out), .Clr(d_ff_1_q), .Q(Decocde), .nQ(out_11));
  D_FF_AS d_ff_as_5 (.Set(in_3), .D(Decocde), .C(and_1_out), .Clr(d_ff_1_q), .Q(Execute), .nQ(out_10));
  not not_21 (not_21_out, register_2_q[11]);
  not not_22 (not_22_out, register_2_q[10]);
  not not_23 (not_23_out, register_2_q[11]);
  not not_24 (not_24_out, register_2_q[10]);
  and and_12 (and_12_out, and_9_out, not_21_out, not_22_out);
  and and_13 (and_13_out, and_9_out, not_23_out, register_2_q[10]);
  and and_14 (and_14_out, and_9_out, register_2_q[11], not_24_out);
  and and_15 (and_15_out, and_9_out, register_2_q[11], register_2_q[10]);
  D_FF_AS d_ff_as_6 (.Set(in_4), .D(Execute), .C(and_1_out), .Clr(d_ff_1_q), .Q(Incrament), .nQ(out_5));
  and and_16 (and_16_out, and_7_out, or_2_out);
  and and_17 (and_17_out, and_6_out, or_2_out);
  and and_18 (and_18_out, and_5_out, or_2_out);
  and and_19 (and_19_out, and_4_out, or_2_out);
  and and_20 (and_20_out, and_12_out, or_2_out);
  and and_21 (and_21_out, and_8_out, or_2_out);
  and and_22 (and_22_out, and_13_out, or_2_out);
  and and_23 (and_23_out, and_14_out, or_2_out);
  and and_24 (and_24_out, and_15_out, or_2_out);
  and and_25 (and_25_out, and_10_out, or_2_out);
  and and_26 (and_26_out, and_11_out, or_2_out);
  not not_25 (not_25_out, out_21);
  not not_26 (not_26_out, out_20);
  and and_27 (and_27_out, and_20_out, out_21);
  and and_28 (and_28_out, and_22_out, not_25_out);
  and and_29 (and_29_out, and_23_out, out_20);
  and and_30 (and_30_out, and_24_out, not_26_out);
  or or_3 (or_3_out, and_21_out, and_20_out, and_22_out, and_23_out, and_24_out);
  or or_4 (or_4_out, and_17_out, and_16_out, and_26_out, and_25_out);
  or or_5 (or_5_out, and_17_out, and_16_out, and_25_out, and_26_out, and_19_out);
  or or_6 (or_6_out, and_27_out, and_28_out, and_29_out, and_30_out, and_21_out);
  or or_7 (or_7_out, and_17_out, and_19_out, and_18_out, or_3_out);
  Multiplexer #(.Bits(8)) multiplexer_1 (
    .sel(not_41_out), .in_0({out_35, out_36, out_37, out_38, out_39, out_40, out_42, out_41}),
    .in_1(register_1_q), .out(multiplexer_1_out));
  Multiplexer #(.Bits(8)) multiplexer_2 (
    .sel(not_43_out), .in_0(blockramdualport_1_d[7:0]), .in_1(register_2_q[7:0]), .out(multiplexer_2_out));
  // Probe on not_43_out
  and and_31 (and_31_out, Incrament, d_ff_as_7_q);
  and and_32 (and_32_out, Execute, or_6_out);
  not not_27 (not_27_out, or_6_out);
  and and_33 (and_33_out, Execute, and_18_out);
  or or_8 (or_8_out, and_26_out, and_19_out, and_17_out, or_3_out);
  or or_9 (or_9_out, Incrament, and_25_out);
  or or_10 (or_10_out, and_19_out, and_18_out);
  and and_34 (and_34_out, Execute, or_5_out);
  or or_11 (or_11_out, and_31_out, and_32_out);
  D_FF_AS d_ff_as_7 (.Set(in_17), .D(not_27_out), .C(or_12_out), .Clr(d_ff_1_q), .Q(d_ff_as_7_q), .nQ(out_22));
  not not_28 (not_28_out, and_33_out);
  not not_29 (not_29_out, not_28_out);
  not not_30 (not_30_out, or_8_out);
  not not_31 (not_31_out[0], not_30_out);
  not not_32 (not_32_out, or_7_out);
  not not_33 (not_31_out[1], not_32_out);
  not not_34 (not_34_out, or_9_out);
  not not_35 (not_35_out, not_34_out);
  not not_36 (not_36_out, and_25_out);
  not not_37 (not_37_out, not_36_out);
  not not_38 (not_38_out, Incrament);
  not not_39 (not_39_out, not_38_out);
  not not_40 (not_40_out, Incrament);
  not not_41 (not_41_out, not_40_out);
  not not_42 (not_42_out, or_4_out);
  not not_43 (not_43_out, not_42_out);
  not not_44 (not_44_out, or_10_out);
  not not_45 (not_45_out, not_44_out);
  not not_46 (not_46_out, Fetch);
  not not_47 (not_47_out, not_46_out);
  not not_48 (not_48_out, not_39_out);
  not not_49 (not_49_out, not_48_out);
  not not_50 (not_50_out, not_49_out);
  not not_51 (not_51_out, not_48_out);
  not not_52 (not_52_out, not_51_out);
  not not_53 (not_53_out, not_48_out);
  not not_54 (not_54_out, not_53_out);
  not not_55 (not_55_out, not_48_out);
  not not_56 (not_56_out, not_55_out);
  not not_57 (not_57_out, not_48_out);
  not not_58 (not_58_out, not_57_out);
  not not_59 (not_59_out, not_48_out);
  not not_60 (not_60_out, not_59_out);
  not not_61 (not_61_out, not_48_out);
  not not_62 (not_62_out, not_61_out);
  not not_63 (not_63_out, not_48_out);
  not not_64 (not_64_out, not_63_out);
  and and_35 (and_42_out[0], multiplexer_1_out[0], multiplexer_2_out[0]);
  and and_36 (and_42_out[1], multiplexer_1_out[1], multiplexer_2_out[1]);
  and and_37 (and_42_out[2], multiplexer_1_out[2], multiplexer_2_out[2]);
  and and_38 (and_42_out[3], multiplexer_1_out[3], multiplexer_2_out[3]);
  and and_39 (and_42_out[4], multiplexer_1_out[4], multiplexer_2_out[4]);
  and and_40 (and_42_out[5], multiplexer_1_out[5], multiplexer_2_out[5]);
  and and_41 (and_42_out[6], multiplexer_1_out[6], multiplexer_2_out[6]);
  and and_42 (and_42_out[7], multiplexer_1_out[7], multiplexer_2_out[7]);
  xor xor_1 (xor_1_out, multiplexer_2_out[0], not_37_out);
  xor xor_2 (xor_2_out, multiplexer_2_out[1], not_37_out);
  xor xor_3 (xor_3_out, multiplexer_2_out[2], not_37_out);
  xor xor_4 (xor_4_out, multiplexer_2_out[3], not_37_out);
  xor xor_5 (xor_5_out, multiplexer_2_out[4], not_37_out);
  xor xor_6 (xor_6_out, multiplexer_2_out[5], not_37_out);
  xor xor_7 (xor_7_out, multiplexer_2_out[6], not_37_out);
  xor xor_8 (xor_8_out, multiplexer_2_out[7], not_37_out);
  and and_43 (and_50_out[0], not_50_out, xor_1_out);
  and and_44 (and_50_out[1], not_52_out, xor_2_out);
  and and_45 (and_50_out[2], not_54_out, xor_3_out);
  and and_46 (and_50_out[3], not_56_out, xor_4_out);
  and and_47 (and_50_out[4], not_58_out, xor_5_out);
  and and_48 (and_50_out[5], not_60_out, xor_6_out);
  and and_49 (and_50_out[6], not_62_out, xor_7_out);
  and and_50 (and_50_out[7], not_64_out, xor_8_out);
  Add #(.Bits(8)) add_1 (.a(multiplexer_1_out), .b(and_50_out), .c_i(not_35_out), .s(add_1_s), .c_o(add_1_c_o));
  Multiplexer #(.Bits(8), .Selector_Bits(2)) multiplexer_3 (
    .sel(not_31_out), .in_0(add_1_s), .in_1(and_42_out), .in_2(multiplexer_1_out), .in_3(multiplexer_2_out),
    .out(multiplexer_3_out));
  nor nor_1 (nor_1_out, multiplexer_3_out[0], multiplexer_3_out[1]);
  nor nor_2 (nor_2_out, multiplexer_3_out[2], multiplexer_3_out[3]);
  nor nor_3 (nor_3_out, multiplexer_3_out[4], multiplexer_3_out[5]);
  nor nor_4 (nor_4_out, multiplexer_3_out[6], multiplexer_3_out[7]);
  and and_51 (and_51_out, nor_1_out, nor_2_out, nor_3_out, nor_4_out);
  Register #(.Bits(8)) register_3 (
    .D(multiplexer_3_out), .C(or_12_out), .en(and_34_out),
    .Q({out_35, out_36, out_37, out_38, out_39, out_40, out_42, out_41}));
  Multiplexer #(.Bits(8)) multiplexer_4 (
    .sel(not_45_out), .in_0(register_1_q), .in_1(register_2_q[7:0]), .out(multiplexer_4_out));
  not not_65 (not_65_out, or_12_out);
  and and_52 (and_52_out, multiplexer_4_out[0], multiplexer_4_out[1]);
  and and_53 (and_53_out, multiplexer_4_out[2], multiplexer_4_out[3]);
  and and_54 (and_54_out, multiplexer_4_out[4], multiplexer_4_out[5]);
  and and_55 (and_55_out, multiplexer_4_out[6], multiplexer_4_out[7]);
  BlockRAMDualPort #(.AddrBits(8), .isProgramMemory("true"), .Bits(16)) blockramdualport_1 (
    .A(multiplexer_4_out),
    .Din({out_24, {7{1'b0}}, out_35, out_36, out_37, out_38, out_39, out_40, out_42, out_41}),
    .str(not_29_out), .C(not_65_out), .D(blockramdualport_1_d));
  // Probe on multiplexer_4_out
  and and_56 (and_56_out, and_52_out, and_53_out);
  and and_57 (and_57_out, and_54_out, and_55_out);
  and and_58 (and_58_out, and_56_out, and_57_out);
  // Probe on {out_35, out_36, out_37, out_38, out_39, out_40, out_42, out_41}
  or or_12 (or_12_out, in_34, and_59_out);
  assign not_66_out = ~{out_35, out_36, out_37, out_38, out_39, out_40, out_42, out_41};  // Not not_66, 8 bits wide
  Terminal terminal_1 (.D(not_66_out), .C(not_65_out), .en(and_58_out));
  and and_59 (and_59_out, clk, in_31);
  // Probe IR on {register_2_q[15:10], out_23, out_24, register_2_q[7:0]}
  // Probe ACC on {out_35, out_36, out_37, out_38, out_39, out_40, out_42, out_41}
  // Probe PC on register_1_q
  // Probe on not_66_out

  assign out_25 = 1'b0;
  assign out_26 = 1'b0;
  assign out_27 = 1'b0;
  assign out_28 = 1'b0;
  assign out_29 = 1'b0;
  assign out_32 = 1'b0;
  assign out_33 = 1'b0;

  // Notes on the sheet:
  //   clk: Hz: 20
endmodule
